# Fritzing sketch Schematic_clock (saved by Fritzing 0.9.3b)

parts:
  Part1 = Arduino Uno (Rev3) - ICSP
  Part2 = Real Time Clock Module - DS1307 RTC Breakout Board
  SP1 = SPEAKER [package=pcb_mount_speaker]

nets:
  N1: Part1.A4/SDA, Part2.SDA
  N2: Part1.A5/SCL, Part2.SCL
  GND: Part1.GND, Part2.GND, SP1.+
  N3: Part1.D3_PWM, SP1.-
  5V: Part1.5V, Part2.5V
